# Fritzing sketch Fritzing Sketch (saved by Fritzing 1.0.4)
perfboards: 1

parts:
  Part1 = HX711 Weighing Sensor Module
  Pico/Pico2_Mod_1 = Raspberry Pi Pico or Pico 2
  S2 = Pushbutton [package="[THT]"]
  S3 = Pushbutton [package="[THT]"]
  Part3 = OLED Monochrome 128x64 0.96 inch [part_number=326]
  Part4 = HX711 Weighing Sensor Module
  Part5 = HX711 Weighing Sensor Module
  Part6 = HX711 Weighing Sensor Module

nets:
  VCC: Part1.VCC, Pico/Pico2_Mod_1.pin_40, Part3.VIN, Part4.VCC, Part5.VCC, Part6.VCC
  GND: Part1.GND, Pico/Pico2_Mod_1.pin_3, Pico/Pico2_Mod_1.pin_8, Pico/Pico2_Mod_1.pin_18, Pico/Pico2_Mod_1.pin_38, Pico/Pico2_Mod_1.pin_42, S2.Pin_3, S2.Pin_4, S3.Pin_3, S3.Pin_4, Part3.GND, Part4.GND, Part5.GND, Part6.GND
  N1: Part1.DO/RX, Pico/Pico2_Mod_1.pin_4
  N2: Part1.CK/TX, Pico/Pico2_Mod_1.pin_5
  N3: Pico/Pico2_Mod_1.pin_6, Part3.MOSI_SDA
  N4: Pico/Pico2_Mod_1.pin_7, Part3.SCLK_SCK
  N5: Pico/Pico2_Mod_1.pin_9, Part4.DO/RX
  N6: Pico/Pico2_Mod_1.pin_10, Part4.CK/TX
  N7: Pico/Pico2_Mod_1.pin_11, Part5.DO/RX
  N8: Pico/Pico2_Mod_1.pin_12, Part5.CK/TX
  N9: Pico/Pico2_Mod_1.pin_14, Part6.DO/RX
  N10: Pico/Pico2_Mod_1.pin_15, Part6.CK/TX
  N11: Pico/Pico2_Mod_1.pin_19, S2.Pin_1, S2.Pin_2
  N12: Pico/Pico2_Mod_1.pin_20, S3.Pin_1, S3.Pin_2

custom parts:
  Raspberry Pi Pico or Pico 2: Raspberry Pi Pico and Pico 2. Based around the RP2040 and RP2350 microcontrollers respectively, Picos are low cost microcontroller device bringing Raspberry Pi quality, cost, and easy of use to the microcontroller space. Jan 2021, Split part in to two versions: tht (this one) and SMD. This one will drill holes for a .1 in header in pcb to allow plugging in the module as well as providing pads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
  OLED Monochrome 128x64 0.96 inch: These displays are small, only about 1" diameter, but very readable due to the high contrast of an OLED display. This display is made of 128x64 individual white OLED pixels, each one is turned on or off by the controller chip. Because the display makes its own light, no backlight is required. This reduces the power required to run the OLED and is why the display has such high contrast; we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
